# Fritzing sketch drums (saved by Fritzing 0.7.10b)
breadboards: 1

parts:
  Pi1 = Adafruit Pi Cobbler
  R1 = 10k Ω Resistor [package=THT]
  R2 = 10k Ω Resistor [package=THT]
  R3 = 10k Ω Resistor [package=THT]
  R4 = 10k Ω Resistor [package=THT]
  J1 = Piezo Speaker
  J2 = Piezo Speaker
  J3 = Piezo Speaker
  J4 = Piezo Speaker

nets:
  N1: Pi1.GND, R1.Pin_0, R2.Pin_0, R3.Pin_0, R4.Pin_0, J1.pin1, J2.pin1, J3.pin1, J4.pin1
  N2: Pi1.#18, R1.Pin_1, J1.pin2
  N3: Pi1.#23, R2.Pin_1, J2.pin2
  N4: Pi1.#24, R3.Pin_1, J3.pin2
  N5: Pi1.#25, R4.Pin_1, J4.pin2

custom parts:
  Adafruit Pi Cobbler: Adafruit Pi Cobbler GPIO Breakout for Raspberry Pi
