# Fritzing sketch glove (saved by Fritzing 0.7.10b)
breadboards: 1

parts:
  Pi1 = Adafruit Pi Cobbler
  R1 = 10k Ω Resistor [package=THT]
  R2 = 10k Ω Resistor [package=THT]
  R3 = 10k Ω Resistor [package=THT]
  R4 = 10k Ω Resistor [package=THT]
  S1 = Tilt Switch [package=THT]
  S2 = Tilt Switch [package=THT]
  S3 = Tilt Switch [package=THT]
  S4 = Tilt Switch [package=THT]

nets:
  N1: Pi1.3V3, S1.Pin_1, S2.Pin_1, S3.Pin_1, S4.Pin_1
  N2: Pi1.#18, R2.Pin_0, S3.Pin_2
  N3: Pi1.#22, R1.Pin_0, S1.Pin_2
  N4: Pi1.#24, R3.Pin_0, S4.Pin_2
  N5: Pi1.#25, R4.Pin_0, S2.Pin_2
  N6: Pi1.PIN25, R1.Pin_1, R2.Pin_1, R3.Pin_1, R4.Pin_1

custom parts:
  Adafruit Pi Cobbler: Adafruit Pi Cobbler GPIO Breakout for Raspberry Pi
