# Fritzing sketch keyboard (saved by Fritzing 0.7.10b)
breadboards: 1

parts:
  Pi1 = Adafruit Pi Cobbler  # not connected
  R1 = 10k Ω Resistor [package=THT]
  R2 = 10k Ω Resistor [package=THT]
  R3 = 10k Ω Resistor [package=THT]
  R4 = 10k Ω Resistor [package=THT]
  S1 = Pushbutton [package="[SMD]"]
  R5 = 10k Ω Resistor [package=THT]
  R6 = 10k Ω Resistor [package=THT]
  R7 = 10k Ω Resistor [package=THT]
  R8 = 10k Ω Resistor [package=THT]
  S2 = Pushbutton [package="[SMD]"]
  S3 = Pushbutton [package="[SMD]"]
  S4 = Pushbutton [package="[SMD]"]
  S5 = Pushbutton [package="[SMD]"]
  S6 = Pushbutton [package="[SMD]"]
  S7 = Pushbutton [package="[SMD]"]
  S8 = Pushbutton [package="[SMD]"]

nets:
  N1: R1.Pin_0, R2.Pin_0, R3.Pin_0, R4.Pin_0, R5.Pin_0, R6.Pin_0, R7.Pin_0, R8.Pin_0
  N2: R1.Pin_1, S1.Pin_1, S1.Pin_2
  N3: R2.Pin_1, S2.Pin_1, S2.Pin_2
  N4: R3.Pin_1, S3.Pin_1
  N5: R4.Pin_1, S4.Pin_1, S4.Pin_2
  N6: S1.Pin_3, S1.Pin_4, S2.Pin_3, S2.Pin_4, S3.Pin_4, S4.Pin_4, S5.Pin_4, S6.Pin_4, S7.Pin_4, S8.Pin_3, S8.Pin_4
  N7: R5.Pin_1, S5.Pin_1
  N8: R6.Pin_1, S6.Pin_1, S6.Pin_2
  N9: R7.Pin_1, S7.Pin_1, S7.Pin_2
  N10: R8.Pin_1, S8.Pin_1, S8.Pin_2

custom parts:
  Adafruit Pi Cobbler: Adafruit Pi Cobbler GPIO Breakout for Raspberry Pi
